# Fritzing sketch protype1 (saved by Fritzing 0.9.3b)
breadboards: 1

parts:
  Q1 = NPN-Transistor [package="TO92 [THT]"]
  Q2 = PNP-Transistor [package="TO92 [THT]"]
  Q3 = NPN-Transistor [package="TO92 [THT]"]
  Q4 = PNP-Transistor [package="TO92 [THT]"]
  R1 = Resistor [tolerance=±5% resistance=220 package=THT]
  R2 = Resistor [tolerance=±5% resistance=220 package=THT]
  R3 = Resistor [tolerance=±5% resistance=220 package=THT]
  R4 = Resistor [tolerance=±5% resistance=220 package=THT]
  R5 = Resistor [tolerance=±5% resistance=220 package=THT]
  LED1 = LED - 5mm [color="Red (633nm)" package="5 mm [THT]"]
  LED2 = LED - 5mm [color="Red (633nm)" package="5 mm [THT]"]

nets:
  N1: Q1.E, Q3.E
  N2: Q1.B, R5.Pin_1
  N3: Q1.C, Q2.C, LED1.cathode, LED2.anode
  N4: Q2.E, Q4.E
  N5: Q2.B, R4.Pin_1
  N6: Q3.B, R3.Pin_0
  N7: Q3.C, Q4.C, R1.Pin_1
  N8: Q4.B, R2.Pin_0
  N9: R1.Pin_0, LED1.anode, LED2.cathode
